# Fritzing sketch Wemos-ADPS9960-Breakout (saved by Fritzing 0.9.3b)
circuit board: 4.5cm x 3cm

parts:
  ADPS_-_9960 = Adafruit APDS-9960 [part_number="Adafruit #3595"]
  WeMos_D1_Mini1 = WeMos D1 Mini
  LED1 = LED - 3mm [color="Red (633nm)" package="3 mm [THT]"]
  R1 = Resistor [tolerance=±5% resistance=220 package=THT]

nets:
  VIN: ADPS_-_9960.VIN, WeMos_D1_Mini1.3V3
  N1: ADPS_-_9960.GND, WeMos_D1_Mini1.G, LED1.cathode
  N2: ADPS_-_9960.SCL, WeMos_D1_Mini1.D1
  N3: ADPS_-_9960.SDA, WeMos_D1_Mini1.D2
  N4: ADPS_-_9960.INT, WeMos_D1_Mini1.D6
  N5: WeMos_D1_Mini1.D7, R1.Pin_1
  N6: LED1.anode, R1.Pin_0

custom parts:
  Adafruit APDS-9960: The APDS9960 from Avago Technologies has an integrated IR LED and driver, along with four directional photodiodes that sense reflected IR energy from the LED. It's proximity detection feature allows it to measure the distance an object is from the front of the sensor (up to a few centimeters) with 8 bit resolution. Since there are four IR sensors, you can measure the changes in light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
