# Fritzing sketch Wemos SSD1306 Wiring (saved by Fritzing 0.9.3b)
circuit board: 3.20668cm x 4.23035cm

parts:
  SSD1306 = Module display OLED I2C 128x64 SSD1306 [package=THT]
  WeMos_D1_Mini1 = WeMos D1 Mini

nets:
  N1: SSD1306.GND, WeMos_D1_Mini1.G
  VCC: SSD1306.VCC, WeMos_D1_Mini1.3V3
  N2: SSD1306.SCL, WeMos_D1_Mini1.D1
  N3: SSD1306.SDA, WeMos_D1_Mini1.D2

custom parts:
  Module display OLED I2C 128x64 SSD1306: Ecran OLED I2C SSD163 de 128x64 avec connexion I2C
